// Logisim project tests.circ as structural Verilog
module Test_7400 (
);

  wire dip_7400_1_p3, dip_7400_1_p6, dip_7400_1_p9, dip_7400_1_p12, Start_out, tip2_1_p2, tip2_1_p3,
       tip2_1_p5, tip2_1_p6, toc4_1_p8;
  wire [1:0] tip2_1_p4;
  wire [3:0] rom_1_data;

  Button Start (.out(Start_out));
  // TIP2 tip2_1: pin names not known; wires that end beside it: Start_out, tip2_1_p2, tip2_1_p3, tip2_1_p4, tip2_1_p5, tip2_1_p6
  // DIP_7400 dip_7400_1: pin names not known; wires that end beside it: tip2_1_p5, tip2_1_p6, dip_7400_1_p3, tip2_1_p5, tip2_1_p6, dip_7400_1_p6, tip2_1_p6, tip2_1_p5, dip_7400_1_p9, tip2_1_p6, tip2_1_p5, dip_7400_1_p12
  ROM #(.addrWidth(2), .dataWidth(4)) rom_1 (.addr(tip2_1_p4), .data(rom_1_data));  // open: sel
  // TOC4 toc4_1: pin names not known; wires that end beside it: dip_7400_1_p3, dip_7400_1_p6, dip_7400_1_p9, dip_7400_1_p12, rom_1_data, tip2_1_p3, tip2_1_p2, toc4_1_p8
  LED Failure (.in(tip2_1_p2));
  LED Success (.in(toc4_1_p8));

  // Notes on the sheet:
  //   contents of rom_1 (hex, n*v repeats v):
  //   f f f
endmodule

module Test_7402 (
);

  wire dip_7402_1_p1, dip_7402_1_p4, dip_7402_1_p7, dip_7402_1_p10, Start_out, tip2_1_p2, tip2_1_p3,
       tip2_1_p5, tip2_1_p6, toc4_1_p8;
  wire [1:0] tip2_1_p4;
  wire [3:0] rom_1_data;

  Button Start (.out(Start_out));
  // TIP2 tip2_1: pin names not known; wires that end beside it: Start_out, tip2_1_p2, tip2_1_p3, tip2_1_p4, tip2_1_p5, tip2_1_p6
  // DIP_7402 dip_7402_1: pin names not known; wires that end beside it: dip_7402_1_p1, tip2_1_p5, tip2_1_p6, dip_7402_1_p4, tip2_1_p5, tip2_1_p6, dip_7402_1_p7, tip2_1_p6, tip2_1_p5, dip_7402_1_p10, tip2_1_p6, tip2_1_p5
  ROM #(.addrWidth(2), .dataWidth(4)) rom_1 (.addr(tip2_1_p4), .data(rom_1_data));  // open: sel
  // TOC4 toc4_1: pin names not known; wires that end beside it: dip_7402_1_p1, dip_7402_1_p4, dip_7402_1_p10, dip_7402_1_p7, rom_1_data, tip2_1_p3, tip2_1_p2, toc4_1_p8
  LED Failure (.in(tip2_1_p2));
  LED Success (.in(toc4_1_p8));

  // Notes on the sheet:
  //   contents of rom_1 (hex, n*v repeats v):
  //   f
endmodule

module Test_7404 (
);

  wire dip_7404_1_p2, dip_7404_1_p4, dip_7404_1_p6, dip_7404_1_p8, dip_7404_1_p10, dip_7404_1_p12, Start_out,
       tip1_1_p2, tip1_1_p3, tip1_1_p4, tip1_1_p5, toc6_1_p10;
  wire [5:5] not_1_out;

  Button Start (.out(Start_out));
  // TIP1 tip1_1: pin names not known; wires that end beside it: Start_out, tip1_1_p2, tip1_1_p3, tip1_1_p4, tip1_1_p5
  not not_1 (not_1_out[5], tip1_1_p4);
  // DIP_7404 dip_7404_1: pin names not known; wires that end beside it: tip1_1_p5, dip_7404_1_p2, tip1_1_p5, dip_7404_1_p4, tip1_1_p5, dip_7404_1_p6, tip1_1_p5, dip_7404_1_p8, tip1_1_p5, dip_7404_1_p10, tip1_1_p5, dip_7404_1_p12
  // TOC6 toc6_1: pin names not known; wires that end beside it: dip_7404_1_p8, dip_7404_1_p10, dip_7404_1_p12, dip_7404_1_p6, dip_7404_1_p4, dip_7404_1_p2, {6{not_1_out[5]}}, tip1_1_p3, tip1_1_p2, toc6_1_p10
  LED Failure (.in(tip1_1_p2));
  LED Success (.in(toc6_1_p10));
endmodule

module Test_7408 (
);

  wire dip_7408_1_p3, dip_7408_1_p6, dip_7408_1_p9, dip_7408_1_p12, Start_out, tip2_1_p2, tip2_1_p3,
       tip2_1_p5, tip2_1_p6, toc4_1_p8;
  wire [1:0] tip2_1_p4;
  wire [3:0] rom_1_data;

  Button Start (.out(Start_out));
  // TIP2 tip2_1: pin names not known; wires that end beside it: Start_out, tip2_1_p2, tip2_1_p3, tip2_1_p4, tip2_1_p5, tip2_1_p6
  // DIP_7408 dip_7408_1: pin names not known; wires that end beside it: tip2_1_p5, tip2_1_p6, dip_7408_1_p3, tip2_1_p5, tip2_1_p6, dip_7408_1_p6, tip2_1_p6, tip2_1_p5, dip_7408_1_p9, tip2_1_p6, tip2_1_p5, dip_7408_1_p12
  ROM #(.addrWidth(2), .dataWidth(4)) rom_1 (.addr(tip2_1_p4), .data(rom_1_data));  // open: sel
  // TOC4 toc4_1: pin names not known; wires that end beside it: dip_7408_1_p3, dip_7408_1_p6, dip_7408_1_p9, dip_7408_1_p12, rom_1_data, tip2_1_p3, tip2_1_p2, toc4_1_p8
  LED Failure (.in(tip2_1_p2));
  LED Success (.in(toc4_1_p8));

  // Notes on the sheet:
  //   contents of rom_1 (hex, n*v repeats v):
  //   0 0 0 f
endmodule

module Test_7410 (
);

  wire dip_7410_1_p6, dip_7410_1_p8, dip_7410_1_p12, Start_out, tip3_1_p2, tip3_1_p3, tip3_1_p5, tip3_1_p6,
       tip3_1_p7, toc3_1_p7;
  wire [2:0] rom_1_data, tip3_1_p4;

  Button Start (.out(Start_out));
  // TIP3 tip3_1: pin names not known; wires that end beside it: Start_out, tip3_1_p2, tip3_1_p3, tip3_1_p4, tip3_1_p5, tip3_1_p6, tip3_1_p7
  // DIP_7410 dip_7410_1: pin names not known; wires that end beside it: tip3_1_p5, tip3_1_p6, tip3_1_p5, tip3_1_p6, tip3_1_p7, dip_7410_1_p6, tip3_1_p7, dip_7410_1_p8, tip3_1_p7, tip3_1_p6, tip3_1_p5, dip_7410_1_p12
  ROM #(.addrWidth(3), .dataWidth(3)) rom_1 (.addr(tip3_1_p4), .data(rom_1_data));  // open: sel
  // TOC3 toc3_1: pin names not known; wires that end beside it: dip_7410_1_p8, dip_7410_1_p6, dip_7410_1_p12, rom_1_data, tip3_1_p3, tip3_1_p2, toc3_1_p7
  LED Failure (.in(tip3_1_p2));
  LED Success (.in(toc3_1_p7));

  // Notes on the sheet:
  //   contents of rom_1 (hex, n*v repeats v):
  //   7*7
endmodule

module Test_7411 (
);

  wire dip_7411_1_p6, dip_7411_1_p8, dip_7411_1_p12, Start_out, tip3_1_p2, tip3_1_p3, tip3_1_p5, tip3_1_p6,
       tip3_1_p7, toc3_1_p7;
  wire [2:0] rom_1_data, tip3_1_p4;

  Button Start (.out(Start_out));
  // TIP3 tip3_1: pin names not known; wires that end beside it: Start_out, tip3_1_p2, tip3_1_p3, tip3_1_p4, tip3_1_p5, tip3_1_p6, tip3_1_p7
  // DIP_7411 dip_7411_1: pin names not known; wires that end beside it: tip3_1_p5, tip3_1_p6, tip3_1_p5, tip3_1_p6, tip3_1_p7, dip_7411_1_p6, tip3_1_p7, dip_7411_1_p8, tip3_1_p7, tip3_1_p6, tip3_1_p5, dip_7411_1_p12
  ROM #(.addrWidth(3), .dataWidth(3)) rom_1 (.addr(tip3_1_p4), .data(rom_1_data));  // open: sel
  // TOC3 toc3_1: pin names not known; wires that end beside it: dip_7411_1_p8, dip_7411_1_p6, dip_7411_1_p12, rom_1_data, tip3_1_p3, tip3_1_p2, toc3_1_p7
  LED Failure (.in(tip3_1_p2));
  LED Success (.in(toc3_1_p7));

  // Notes on the sheet:
  //   contents of rom_1 (hex, n*v repeats v):
  //   7*0 7
endmodule

module Test_7420 (
);

  wire dip_7420_1_p5, dip_7420_1_p10, Start_out, tip4_1_p2, tip4_1_p3, tip4_1_p5, tip4_1_p6, tip4_1_p7,
       tip4_1_p8, toc2_1_p6;
  wire [1:0] rom_1_data;
  wire [3:0] tip4_1_p4;

  Button Start (.out(Start_out));
  // TIP4 tip4_1: pin names not known; wires that end beside it: Start_out, tip4_1_p2, tip4_1_p3, tip4_1_p4, tip4_1_p5, tip4_1_p6, tip4_1_p7, tip4_1_p8
  // DIP_7420 dip_7420_1: pin names not known; wires that end beside it: tip4_1_p5, tip4_1_p6, tip4_1_p7, tip4_1_p8, dip_7420_1_p5, tip4_1_p8, tip4_1_p7, tip4_1_p6, tip4_1_p5, dip_7420_1_p10
  ROM #(.addrWidth(4), .dataWidth(2)) rom_1 (.addr(tip4_1_p4), .data(rom_1_data));  // open: sel
  // TOC2 toc2_1: pin names not known; wires that end beside it: dip_7420_1_p5, dip_7420_1_p10, rom_1_data, tip4_1_p3, tip4_1_p2, toc2_1_p6
  LED Failure (.in(tip4_1_p2));
  LED Success (.in(toc2_1_p6));

  // Notes on the sheet:
  //   contents of rom_1 (hex, n*v repeats v):
  //   15*3
endmodule

module Test_7421 (
);

  wire dip_7421_1_p5, dip_7421_1_p10, Start_out, tip4_1_p2, tip4_1_p3, tip4_1_p5, tip4_1_p6, tip4_1_p7,
       tip4_1_p8, toc2_1_p6;
  wire [1:0] rom_1_data;
  wire [3:0] tip4_1_p4;

  Button Start (.out(Start_out));
  // TIP4 tip4_1: pin names not known; wires that end beside it: Start_out, tip4_1_p2, tip4_1_p3, tip4_1_p4, tip4_1_p5, tip4_1_p6, tip4_1_p7, tip4_1_p8
  // DIP_7421 dip_7421_1: pin names not known; wires that end beside it: tip4_1_p5, tip4_1_p6, tip4_1_p7, tip4_1_p8, dip_7421_1_p5, tip4_1_p8, tip4_1_p7, tip4_1_p6, tip4_1_p5, dip_7421_1_p10
  ROM #(.addrWidth(4), .dataWidth(2)) rom_1 (.addr(tip4_1_p4), .data(rom_1_data));  // open: sel
  // TOC2 toc2_1: pin names not known; wires that end beside it: dip_7421_1_p5, dip_7421_1_p10, rom_1_data, tip4_1_p3, tip4_1_p2, toc2_1_p6
  LED Failure (.in(tip4_1_p2));
  LED Success (.in(toc2_1_p6));

  // Notes on the sheet:
  //   contents of rom_1 (hex, n*v repeats v):
  //   15*0 3
endmodule

module Test_7425 (
);

  wire dip_7425_1_p5, dip_7425_1_p10, Start_out, tip4_1_p2, tip4_1_p3, tip4_1_p5, tip4_1_p6, tip4_1_p7,
       tip4_1_p8, toc2_1_p6;
  wire [1:0] rom_1_data;
  wire [3:0] tip4_1_p4;

  Button Start (.out(Start_out));
  // TIP4 tip4_1: pin names not known; wires that end beside it: Start_out, tip4_1_p2, tip4_1_p3, tip4_1_p4, tip4_1_p5, tip4_1_p6, tip4_1_p7, tip4_1_p8
  // DIP_7425 dip_7425_1: pin names not known; wires that end beside it: tip4_1_p5, tip4_1_p6, tip4_1_p7, tip4_1_p8, dip_7425_1_p5, tip4_1_p8, tip4_1_p7, tip4_1_p6, tip4_1_p5, dip_7425_1_p10
  ROM #(.addrWidth(4), .dataWidth(2)) rom_1 (.addr(tip4_1_p4), .data(rom_1_data));  // open: sel
  // TOC2 toc2_1: pin names not known; wires that end beside it: dip_7425_1_p5, dip_7425_1_p10, rom_1_data, tip4_1_p3, tip4_1_p2, toc2_1_p6
  LED Failure (.in(tip4_1_p2));
  LED Success (.in(toc2_1_p6));

  // Notes on the sheet:
  //   contents of rom_1 (hex, n*v repeats v):
  //   3
endmodule

module Test_7427 (
);

  wire dip_7427_1_p6, dip_7427_1_p8, dip_7427_1_p12, Start_out, tip3_1_p2, tip3_1_p3, tip3_1_p5, tip3_1_p6,
       tip3_1_p7, toc3_1_p7;
  wire [2:0] rom_1_data, tip3_1_p4;

  Button Start (.out(Start_out));
  // TIP3 tip3_1: pin names not known; wires that end beside it: Start_out, tip3_1_p2, tip3_1_p3, tip3_1_p4, tip3_1_p5, tip3_1_p6, tip3_1_p7
  // DIP_7427 dip_7427_1: pin names not known; wires that end beside it: tip3_1_p5, tip3_1_p6, tip3_1_p5, tip3_1_p6, tip3_1_p7, dip_7427_1_p6, tip3_1_p7, dip_7427_1_p8, tip3_1_p7, tip3_1_p6, tip3_1_p5, dip_7427_1_p12
  ROM #(.addrWidth(3), .dataWidth(3)) rom_1 (.addr(tip3_1_p4), .data(rom_1_data));  // open: sel
  // TOC3 toc3_1: pin names not known; wires that end beside it: dip_7427_1_p8, dip_7427_1_p6, dip_7427_1_p12, rom_1_data, tip3_1_p3, tip3_1_p2, toc3_1_p7
  LED Failure (.in(tip3_1_p2));
  LED Success (.in(toc3_1_p7));

  // Notes on the sheet:
  //   contents of rom_1 (hex, n*v repeats v):
  //   7
endmodule

module Test_7432 (
);

  wire dip_7432_1_p3, dip_7432_1_p6, dip_7432_1_p9, dip_7432_1_p12, Start_out, tip2_1_p2, tip2_1_p3,
       tip2_1_p5, tip2_1_p6, toc4_1_p8;
  wire [1:0] tip2_1_p4;
  wire [3:0] rom_1_data;

  Button Start (.out(Start_out));
  // TIP2 tip2_1: pin names not known; wires that end beside it: Start_out, tip2_1_p2, tip2_1_p3, tip2_1_p4, tip2_1_p5, tip2_1_p6
  // DIP_7432 dip_7432_1: pin names not known; wires that end beside it: tip2_1_p5, tip2_1_p6, dip_7432_1_p3, tip2_1_p5, tip2_1_p6, dip_7432_1_p6, tip2_1_p6, tip2_1_p5, dip_7432_1_p9, tip2_1_p6, tip2_1_p5, dip_7432_1_p12
  ROM #(.addrWidth(2), .dataWidth(4)) rom_1 (.addr(tip2_1_p4), .data(rom_1_data));  // open: sel
  // TOC4 toc4_1: pin names not known; wires that end beside it: dip_7432_1_p3, dip_7432_1_p6, dip_7432_1_p9, dip_7432_1_p12, rom_1_data, tip2_1_p3, tip2_1_p2, toc4_1_p8
  LED Failure (.in(tip2_1_p2));
  LED Success (.in(toc4_1_p8));

  // Notes on the sheet:
  //   contents of rom_1 (hex, n*v repeats v):
  //   0 f f f
endmodule

module Test_7474_TODO (
);

  wire and_1_out, and_2_out, clock_1_out, dip_7474_1_p5, not_1_out, not_2_out, xnor_1_out, xnor_2_out;
  wire [4:0] counter_1_q;

  Counter #(.width(5), .max('h1f)) counter_1 (
    .count(1'b1), .Q(counter_1_q), .clk(clock_1_out));  // open: load, D, carry, clr
  Clock clock_1 (.out(clock_1_out));
  // DIP_7474 dip_7474_1: pin names not known; wires that end beside it: counter_1_q[3], counter_1_q[2], counter_1_q[1], counter_1_q[4], dip_7474_1_p5, counter_1_q[0], counter_1_q[1], counter_1_q[2], counter_1_q[3], counter_1_q[4]
  not not_1 (not_1_out, counter_1_q[3]);
  not not_2 (not_2_out, counter_1_q[4]);
  and and_1 (and_1_out, not_1_out, counter_1_q[4]);
  and and_2 (and_2_out, counter_1_q[3], not_2_out);
  xnor xnor_1 (xnor_1_out, and_1_out, dip_7474_1_p5);
  xnor xnor_2 (xnor_2_out, and_2_out, dip_7474_1_p5);

  // Notes on the sheet:
  //   If SET is LOW and CLR is HIGH, Q must be HIGH
  //   If CLR is LOW, Q must be LOW
endmodule

module Test_4786 (
);

  wire and_1_out, clock_1_out, dip_7486_1_p3, dip_7486_1_p6, dip_7486_1_p9, dip_7486_1_p12, xnor_1_out,
       xnor_2_out, xnor_3_out, xnor_4_out, xor_1_out;
  wire [1:0] counter_1_q;

  Clock clock_1 (.out(clock_1_out));
  Counter #(.width(2), .max('h3)) counter_1 (
    .count(1'b1), .Q(counter_1_q), .clk(clock_1_out));  // open: load, D, carry, clr
  // DIP_7486 dip_7486_1: pin names not known; wires that end beside it: counter_1_q[0], counter_1_q[1], dip_7486_1_p3, counter_1_q[0], counter_1_q[1], dip_7486_1_p6, counter_1_q[1], counter_1_q[0], dip_7486_1_p9, counter_1_q[1], counter_1_q[0], dip_7486_1_p12
  xor xor_1 (xor_1_out, counter_1_q[0], counter_1_q[1]);
  xnor xnor_1 (xnor_1_out, xor_1_out, dip_7486_1_p9);
  xnor xnor_2 (xnor_2_out, xor_1_out, dip_7486_1_p12);
  xnor xnor_3 (xnor_3_out, xor_1_out, dip_7486_1_p3);
  xnor xnor_4 (xnor_4_out, xor_1_out, dip_7486_1_p6);
  LED led_1 (.in(and_1_out));
  and and_1 (and_1_out, xnor_1_out, xnor_2_out, xnor_3_out, xnor_4_out);
endmodule

module Test_74147 (
);

  wire and_1_out, clock_1_out, not_1_out, not_2_out, not_3_out, not_4_out, not_5_out, not_6_out, not_7_out,
       not_8_out, not_9_out, not_10_out, not_11_out, not_12_out, not_13_out, not_14_out, undriven,
       undriven_2, undriven_3, undriven_4, xnor_1_out, xnor_2_out, xnor_3_out, xnor_4_out;
  wire [3:0] counter_1_q, priority_encoder_1_out;
  wire [9:0] shifter_1_out;

  Clock clock_1 (.out(clock_1_out));
  Shifter #(.width(10), .shift("rl")) shifter_1 (.in(10'h1ff), .\dist (counter_1_q), .out(shifter_1_out));
  Counter #(.width(4), .max('hf)) counter_1 (
    .count(1'b1), .Q(counter_1_q), .clk(clock_1_out));  // open: load, D, carry, clr
  not not_1 (not_1_out, shifter_1_out[9]);
  not not_2 (not_2_out, shifter_1_out[0]);
  not not_3 (not_3_out, shifter_1_out[1]);
  not not_4 (not_4_out, shifter_1_out[2]);
  not not_5 (not_5_out, shifter_1_out[3]);
  not not_6 (not_6_out, shifter_1_out[4]);
  not not_7 (not_7_out, shifter_1_out[5]);
  not not_8 (not_8_out, shifter_1_out[6]);
  not not_9 (not_9_out, shifter_1_out[7]);
  not not_10 (not_10_out, shifter_1_out[8]);
  Priority_Encoder #(.select(4)) priority_encoder_1 (
    .in0(not_1_out), .in1(not_2_out), .in2(not_3_out), .in3(not_4_out), .in4(not_5_out), .in5(not_6_out),
    .in6(not_7_out), .in7(not_8_out), .in8(not_9_out), .in9(not_10_out), .out(priority_encoder_1_out));  // open: in10, in11, in12, in13, in14, in15, gs, en_out, en_in
  not not_11 (not_11_out, priority_encoder_1_out[2]);
  not not_12 (not_12_out, priority_encoder_1_out[1]);
  not not_13 (not_13_out, priority_encoder_1_out[3]);
  not not_14 (not_14_out, priority_encoder_1_out[0]);
  xnor xnor_1 (xnor_1_out, undriven_4, not_14_out);
  xnor xnor_2 (xnor_2_out, undriven_2, not_12_out);
  xnor xnor_3 (xnor_3_out, undriven, not_11_out);
  xnor xnor_4 (xnor_4_out, undriven_3, not_13_out);
  LED led_1 (.in(and_1_out));
  and and_1 (and_1_out, xnor_1_out, xnor_2_out, xnor_3_out, xnor_4_out);
endmodule

module Test_74283 (
);

  wire adder_1_cout, and_1_out, clock_1_out, dip_74283_1_p1, dip_74283_1_p4, dip_74283_1_p10,
       dip_74283_1_p13, dip_74283_1_p14, xnor_1_out, xnor_2_out, xnor_3_out, xnor_4_out, xnor_5_out;
  wire [3:0] adder_1_out, counter_1_q, counter_1_q_2;
  wire [8:8] counter_1_q_3;

  Clock clock_1 (.out(clock_1_out));
  Counter #(.width(9), .max('h1ff)) counter_1 (
    .count(1'b1), .Q({counter_1_q_3[8], counter_1_q_2, counter_1_q}), .clk(clock_1_out));  // open: load, D, carry, clr
  Adder #(.width(4)) adder_1 (
    .a(counter_1_q), .b(counter_1_q_2), .out(adder_1_out), .cin(counter_1_q_3[8]), .cout(adder_1_cout));
  // DIP_74283 dip_74283_1: pin names not known; wires that end beside it: dip_74283_1_p1, counter_1_q[1], counter_1_q_2[1], dip_74283_1_p4, counter_1_q[0], counter_1_q_2[0], counter_1_q_3[8], counter_1_q_2[2], counter_1_q[2], dip_74283_1_p10, counter_1_q_2[3], counter_1_q[3], dip_74283_1_p13, dip_74283_1_p14
  xnor xnor_1 (xnor_1_out, dip_74283_1_p4, adder_1_out[0]);
  xnor xnor_2 (xnor_2_out, dip_74283_1_p1, adder_1_out[1]);
  xnor xnor_3 (xnor_3_out, dip_74283_1_p10, adder_1_out[2]);
  xnor xnor_4 (xnor_4_out, dip_74283_1_p13, adder_1_out[3]);
  xnor xnor_5 (xnor_5_out, dip_74283_1_p14, adder_1_cout);
  and and_1 (and_1_out, xnor_1_out, xnor_2_out, xnor_3_out, xnor_4_out, xnor_5_out);
  LED led_1 (.in(and_1_out));
endmodule

module Test_744075 (
);

  wire and_1_out, clock_1_out, dip_744075_1_p6, dip_744075_1_p10, dip_744075_1_p11, or_1_out, xnor_1_out,
       xnor_2_out, xnor_3_out;
  wire [2:0] counter_1_q;

  Clock clock_1 (.out(clock_1_out));
  Counter #(.width(3), .max('h7)) counter_1 (
    .count(1'b1), .Q(counter_1_q), .clk(clock_1_out));  // open: load, D, carry, clr
  // DIP_744075 dip_744075_1: pin names not known; wires that end beside it: counter_1_q[0], counter_1_q[1], counter_1_q[0], counter_1_q[1], counter_1_q[2], dip_744075_1_p6, counter_1_q[2], counter_1_q[1], counter_1_q[0], dip_744075_1_p10, dip_744075_1_p11, counter_1_q[2]
  or or_1 (or_1_out, counter_1_q[0], counter_1_q[1], counter_1_q[2]);
  xnor xnor_1 (xnor_1_out, or_1_out, dip_744075_1_p10);
  xnor xnor_2 (xnor_2_out, or_1_out, dip_744075_1_p11);
  xnor xnor_3 (xnor_3_out, or_1_out, dip_744075_1_p6);
  LED led_1 (.in(and_1_out));
  and and_1 (and_1_out, xnor_1_out, xnor_2_out, xnor_3_out);
endmodule

module Test_744511 (
  input  LE,
  input  LT_,
  input  BL_
);

  wire clock_1_out, dip_744511_1_p8, dip_744511_1_p9, dip_744511_1_p10, dip_744511_1_p11, dip_744511_1_p12,
       dip_744511_1_p13, dip_744511_1_p14;
  wire [3:0] counter_1_q;

  Clock clock_1 (.out(clock_1_out));
  Counter #(.width(4), .max('hf)) counter_1 (
    .count(1'b1), .Q(counter_1_q), .clk(clock_1_out));  // open: load, D, carry, clr
  // DIP_744511 dip_744511_1: pin names not known; wires that end beside it: counter_1_q[1], counter_1_q[2], LT_, BL_, LE, counter_1_q[3], counter_1_q[0], dip_744511_1_p8, dip_744511_1_p9, dip_744511_1_p10, dip_744511_1_p11, dip_744511_1_p12, dip_744511_1_p13, dip_744511_1_p14
  _7_Segment_Display u_7_segment_display_1 (
    .g(dip_744511_1_p9), .f(dip_744511_1_p8), .a(dip_744511_1_p10), .b(dip_744511_1_p11),
    .e(dip_744511_1_p14), .d(dip_744511_1_p13), .c(dip_744511_1_p12));  // open: dp
endmodule
